# Fritzing sketch display 16x2 (saved by Fritzing 0.9.3b)
breadboards: 1

parts:
  U1 = LCD-16X2 [package=lcd-16x2]
  Componente1 = Arduino Uno (Rev3)
  R1 = Rotary Potentiometer (Small) [maximum_resistance=100kΩ package=THT]
  R2 = Resistor [tolerance=±5% resistance=220 package=THT]
  R3 = Photocell (LDR) [package=THT]

nets:
  VSS: U1.VSS, U1.R_W, U1.K, Componente1.GND, R1.leg2, R2.Pin_0
  VDD: U1.VDD, U1.A, Componente1.5V, R1.leg1, R3.pin_0
  N1: U1.VO, R1.wiper
  N2: U1.RS, Componente1.D12/MISO
  N3: U1.E, Componente1.D11_PWM/MOSI
  N4: U1.DB4, Componente1.D5_PWM
  N5: U1.DB5, Componente1.D4
  N6: U1.DB6, Componente1.D3_PWM
  N7: U1.DB7, Componente1.D2
  N8: Componente1.A0, R2.Pin_1, R3.pin_1
