# Fritzing sketch pwm (saved by Fritzing 0.9.3b)
breadboards: 1

parts:
  LED1 = LED - 5mm [color="Red (633nm)" package="5 mm [THT]"]
  Componente1 = Arduino Uno (Rev3)
  R1 = Resistor [tolerance=±5% resistance=220 package=THT]
  R2 = Resistor [tolerance=±5% resistance=1k package=THT]
  Q1 = npn-Powertransistor [package="TO220 [THT]"]
  D1 = Rectifier Diode [part_number=1N4001 package="300 mil [THT]"]
  VCC1 = 4 x AAA Battery Mount
  M1 = DC Motor

nets:
  N1: LED1.cathode, R1.Pin_0
  N2: LED1.anode, Componente1.D11_PWM/MOSI
  N3: Componente1.GND, R1.Pin_1, Q1.emitter, VCC1.-
  N4: Componente1.D3_PWM, R2.Pin_0
  N5: R2.Pin_1, Q1.base
  N6: Q1.collector, D1.anode, M1.pin_2
  N7: D1.cathode, VCC1.+, M1.pin_1
