# Fritzing sketch CaptacaoAguaing (saved by Fritzing 0.9.3b)
breadboards: 1

parts:
  Componente1 = Arduino Uno (Rev3)
  YF-S201_Flow_Meter1 = YF-S201 Water Flow Meter
  R1 = Resistor [tolerance=±5% resistance=1k package=THT]
  R2 = Resistor [tolerance=±5% resistance=1k package=THT]

nets:
  N1: Componente1.D2, YF-S201_Flow_Meter1.SIG
  N2: Componente1.D7, R1.Pin_0
  N3: YF-S201_Flow_Meter1.GND, R1.Pin_1, R2.Pin_1

notes:
  BOIA DE NÍVEL VERTICAL

custom parts:
  YF-S201 Water Flow Meter: The YF-S201 Flow Meter. The input voltage is 5V to 24V (DC).
